// Logisim project Magic1_Top.circ as structural Verilog: 1 circuit, main circuit Magic1
module Magic1 (
  output [15:0] out_1,
  output [21:0] out_2
);

  wire front_panel_1_fp_ram, front_panel_1_manual_clk, front_panel_1_nbp_reset, front_panel_1_ndma_req,
       front_panel_1_nfp_write, front_panel_1_nstop_clk, front_panel_1_zinit_inst, ic_74138_1_y2,
       ic_74138_1_y4, nand_1_out, not_1_out, not_2_out, U3C_out, U5B_out, U5D_out, U26A_out, U26B_out,
       U27A_out;
  wire [1:0] front_panel_1_clock_select, ir_decode_1_immval, ir_decode_1_ner_ctlbus;
  wire [3:0] front_panel_1_fp_l;
  wire [5:0] pull_resistor_1_node;
  wire [6:0] ir_decode_1_xl_ctlbus;
  wire [7:0] ir_decode_1_ir, ir_decode_1_msw_flags, ram_rom_1_dbus, register_1_q, regs_1_d;
  wire [11:0] ir_decode_1_nel_ctlbus;
  wire [13:0] ir_decode_1_ioclk;
  wire [15:0] ir_decode_1_l, ir_decode_1_z, regs_1_mar, regs_1_r;
  wire [20:0] ir_decode_1_l_ctlbus;

  Register #(.trigger("low")) register_1 (.D(ram_rom_1_dbus), .en(1'b1), .clk(U5B_out), .Q(register_1_q));  // open: clr
  Hex_Digit_Display hex_digit_display_1 (.value(register_1_q[7:4]));  // open: dp
  Hex_Digit_Display hex_digit_display_2 (.value(register_1_q[3:0]));  // open: dp
  or U5B (U5B_out, ir_decode_1_ioclk[10], ic_74138_1_y4);
  not not_1 (not_1_out, U5B_out);
  // NoConnect on ir_decode_1_msw_flags[2]
  Pull_Resistor #(.pull(1)) pull_resistor_1 (.node(pull_resistor_1_node[0]));
  Pull_Resistor #(.pull(1)) pull_resistor_2 (.node(pull_resistor_1_node[1]));
  Pull_Resistor #(.pull(1)) pull_resistor_3 (.node(pull_resistor_1_node[2]));
  Pull_Resistor #(.pull(1)) pull_resistor_4 (.node(pull_resistor_1_node[3]));
  Pull_Resistor #(.pull(1)) pull_resistor_5 (.node(pull_resistor_1_node[4]));
  Pull_Resistor #(.pull(1)) pull_resistor_6 (.node(pull_resistor_1_node[5]));
  Front_Panel front_panel_1 (
    .MANUAL_CLK(front_panel_1_manual_clk), .nDMA_REQ(front_panel_1_ndma_req), .FP_L(front_panel_1_fp_l),
    .nFP_WRITE(front_panel_1_nfp_write), .ZINIT_INST(front_panel_1_zinit_inst),
    .MEMORY(ir_decode_1_ioclk[2]), .nBP_RESET(front_panel_1_nbp_reset),
    .CLOCK_SELECT(front_panel_1_clock_select), .FP_RAM(front_panel_1_fp_ram),
    .nSTOP_CLK(front_panel_1_nstop_clk), .MSWP(ir_decode_1_msw_flags[0]), .MSWE(ir_decode_1_msw_flags[1]),
    .MSWM(ir_decode_1_msw_flags[3]), .MSWV(ir_decode_1_msw_flags[4]), .MSWC(ir_decode_1_msw_flags[6]),
    .MSWS(ir_decode_1_msw_flags[5]), .MSWZ(ir_decode_1_msw_flags[7]), .MAR(regs_1_mar), .L_PCODE(not_1_out),
    .CLKS(ir_decode_1_ioclk[5]), .XINIT_INST(ir_decode_1_ioclk[4]), .nRW(ir_decode_1_ioclk[9]),
    .nPSEL2(ic_74138_1_y2), .A(out_2), .DBUS(ram_rom_1_dbus), .nDMA_ACK(ir_decode_1_ioclk[8]),
    .L(ir_decode_1_l), .L_FPL(ir_decode_1_l_ctlbus[6]), .nNW(ir_decode_1_ioclk[6]),
    .MEMREF(ir_decode_1_ioclk[1]), .nWR(ir_decode_1_ioclk[10]), .INIT_INST(ir_decode_1_ioclk[3]),
    .nNP(ir_decode_1_ioclk[7]), .nIRQ5(pull_resistor_1_node[5]), .nIRQ4(pull_resistor_1_node[4]),
    .nIRQ3(pull_resistor_1_node[3]), .nIRQ2(pull_resistor_1_node[2]), .nIRQ1(pull_resistor_1_node[1]),
    .nIRQ0(pull_resistor_1_node[0]), .nHALT(ir_decode_1_ioclk[12]), .nRESET(ir_decode_1_ioclk[13]),
    .IDE_DRV(1'b1), .IR(ir_decode_1_ir));
  // NoConnect on front_panel_1_zinit_inst
  or U5D (U5D_out, ir_decode_1_ioclk[0], ir_decode_1_ioclk[9]);
  IR_DECODE ir_decode_1 (
    .nHALT(ir_decode_1_ioclk[12]), .nER_CTLBUS(ir_decode_1_ner_ctlbus), .nEL_CTLBUS(ir_decode_1_nel_ctlbus),
    .CLKS(ir_decode_1_ioclk[5]), .INIT_INST(ir_decode_1_ioclk[3]), .nWR(ir_decode_1_ioclk[10]),
    .IMMVAL(ir_decode_1_immval), .L_CTLBUS(ir_decode_1_l_ctlbus), .IR(ir_decode_1_ir), .L(ir_decode_1_l),
    .T(out_1), .nWAIT(ir_decode_1_ioclk[11]), .MEMREF(ir_decode_1_ioclk[1]), .nNW(ir_decode_1_ioclk[6]),
    .nNP(ir_decode_1_ioclk[7]), .A(out_2), .MEMORY(ir_decode_1_ioclk[2]), .nRW(ir_decode_1_ioclk[9]),
    .XL_CTLBUS(ir_decode_1_xl_ctlbus), .XINIT_INST(ir_decode_1_ioclk[4]), .Z(ir_decode_1_z),
    .nDMA_ACK(ir_decode_1_ioclk[8]), .nRESET(ir_decode_1_ioclk[13]), .MSW_FLAGS(ir_decode_1_msw_flags),
    .IOCLK(ir_decode_1_ioclk[0]), .nFP_WRITE(front_panel_1_nfp_write), .DBUS(ram_rom_1_dbus),
    .nIRQ(pull_resistor_1_node), .MAR(regs_1_mar), .R(regs_1_r), .nDMA_REQ(front_panel_1_ndma_req),
    .nSTOP_CLK(front_panel_1_nstop_clk), .CLOCK_SELECT(front_panel_1_clock_select),
    .MANUAL_CLK(front_panel_1_manual_clk), .nBP_RESET(front_panel_1_nbp_reset), .FP_L(front_panel_1_fp_l));
  RAM_ROM ram_rom_1 (
    .nWE(ir_decode_1_ioclk[10]), .A(out_2), .nOE(U5D_out), .FP_RAM(front_panel_1_fp_ram),
    .MEMORY(ir_decode_1_ioclk[2]), .DBUS(ram_rom_1_dbus));
  nor U26A (U26A_out, out_2[0], out_2[1], out_2[2]);
  nor U26B (U26B_out, out_2[3], out_2[4], out_2[5]);
  nand nand_1 (nand_1_out, out_2[6], out_2[7], out_2[8], out_2[9], out_2[10], out_2[11], out_2[12], out_2[13], out_2[14]);
  nand U27A (U27A_out, U26A_out, U26B_out);
  not not_2 (not_2_out, ir_decode_1_ioclk[1]);
  REGS regs_1 (
    .L(ir_decode_1_l), .MAR(regs_1_mar), .D(regs_1_d), .DBUS(ram_rom_1_dbus), .R(regs_1_r),
    .nDMA_ACK(ir_decode_1_ioclk[8]), .nRW(ir_decode_1_ioclk[9]), .Z(ir_decode_1_z),
    .XL_CTLBUS(ir_decode_1_xl_ctlbus), .nRESET(ir_decode_1_ioclk[13]), .IMMVAL(ir_decode_1_immval),
    .nER_CTLBUS(ir_decode_1_ner_ctlbus), .nEL_CTLBUS(ir_decode_1_nel_ctlbus), .L_CTLBUS(ir_decode_1_l_ctlbus));
  // NoConnect on regs_1_d
  nor U3C (U3C_out, U27A_out, nand_1_out, ir_decode_1_ioclk[2]);
  IC_74138 ic_74138_1 (
    .Y2(ic_74138_1_y2), .Y4(ic_74138_1_y4), .A2(out_2[15]), .A0(out_2[17]), .OE1(not_2_out), .OE2(not_2_out),
    .OE3(U3C_out), .A1(out_2[16]));  // open: Y0, Y1, Y3, Y5, Y6, Y7
endmodule
