// Logisim project Microcode.circ as structural Verilog: 1 circuit, main circuit main
module main (
  input  CLK_M,
  input  nFP_WRITE,
  input  nRESET,
  input  nDMA_ACQ,
  input  [3:0] ENCODER,
  input  [7:0] DBUS,
  input  INIT_INST,
  input  MSWC,
  input  MSWZ,
  input  FAULT_PENDING,
  input  MSWS,
  input  nDO_BRANCH,
  input  MSWV,
  output [3:0] LATCH,
  output XL_MAR,
  output R_RW,
  output XL_MDR_LO,
  output XL_MDR_HI,
  output nE_MDR_LO,
  output PRIV,
  output XL_MODE,
  output nE_MDR_HI,
  output XL_PAGING,
  output [3:0] MISC,
  output [3:0] EL,
  output [1:0] ER,
  output [1:0] RIMM_VAL,
  output [7:0] IR,
  output ALUOP_SZ,
  output [1:0] ALU_OP,
  output USE_CARRY,
  output LATCH_SZ,
  output RUSER_PTB,
  output CODE_PTB
);

  wire NEGATE_BR, not_1_out, U11_y, U12A_out, U12B_out, U13A_out, U13B_out, U13C_out, U14A_out, U14D_out,
       U14E_out, U21_out, U24_out, U61B_out;
  wire [0:0] U44B_out;
  wire [7:0] NEXT_INST;
  wire [8:0] U61D_out;
  wire [16:15] register_1_q;
  wire [39:0] rom_1_data;

  not U14E (U14E_out, MSWC);
  xor U12B (U12B_out, MSWS, MSWV);
  IC_74273 ic_74273_1 (
    .Y2(IR[1]), .Y3(IR[2]), .Y1(IR[0]), .Y4(IR[3]), .Y5(IR[4]), .Y6(IR[5]), .Y7(IR[6]), .Y8(IR[7]),
    .D2(DBUS[1]), .D3(DBUS[2]), .D1(DBUS[0]), .D4(DBUS[3]), .D5(DBUS[4]), .D6(DBUS[5]), .D7(DBUS[6]),
    .D8(DBUS[7]), .CLK(INIT_INST), .CLR(1'b1));
  or U13C (U13C_out, U14E_out, MSWZ);
  or U13B (U13B_out, U12B_out, MSWZ);
  not U14A (U14A_out, MSWZ);
  IC_74151 U11 (
    .Y(U11_y), .C(U12B_out), .D(U13B_out), .E(U14E_out), .A(MSWZ), .F(U13C_out), .G(MSWZ), .J(U14A_out),
    .S0(IR[3]), .S1(IR[2]), .S2(IR[1]), .OE(1'b0), .B(MSWZ));  // open: Z
  nand U24 (U24_out, NEXT_INST[0], NEXT_INST[1], NEXT_INST[2], NEXT_INST[3], NEXT_INST[4], NEXT_INST[5], NEXT_INST[6], NEXT_INST[7]);
  xor U12A (U12A_out, NEGATE_BR, U11_y);
  Multiplexer #(.enable("false"), .select(2), .width(8)) multiplexer_1 (
    .in0({4'b0000, ENCODER[0], ENCODER[1], ENCODER[2], ENCODER[3]}),
    .in1({IR[0], IR[1], IR[2], IR[3], IR[4], IR[5], IR[6], IR[7]}),
    .in2({4'b0000, ENCODER[0], ENCODER[1], ENCODER[2], ENCODER[3]}),
    .in3({NEXT_INST[0], NEXT_INST[1], NEXT_INST[2], NEXT_INST[3], NEXT_INST[4], NEXT_INST[5], NEXT_INST[6], NEXT_INST[7]}),
    .out(U61D_out[7:0]), .sel({U61D_out[8], U44B_out[0]}));
  or U61D (U61D_out[8], U24_out, FAULT_PENDING);
  not U14D (U14D_out, FAULT_PENDING);
  or U13A (U13A_out, nDO_BRANCH, U12A_out);
  or U21 (U21_out, NEXT_INST[0], NEXT_INST[1], NEXT_INST[2], NEXT_INST[3], NEXT_INST[4], NEXT_INST[5], NEXT_INST[6], NEXT_INST[7]);
  and U44B (U44B_out[0], U14D_out, U13A_out, U21_out);
  ROM #(.addrWidth(9), .dataWidth(40)) rom_1 (.addr(U61D_out), .data(rom_1_data));
  Register #(.width(40)) register_1 (
    .D(rom_1_data), .en(1'b1), .clk(CLK_M),
    .Q({CODE_PTB, RUSER_PTB, NEGATE_BR, LATCH_SZ, USE_CARRY, ALU_OP[0], ALU_OP[1], ALUOP_SZ, RIMM_VAL[0], RIMM_VAL[1], ER[0], ER[1], EL, MISC, XL_PAGING, XL_MODE, PRIV, register_1_q, XL_MDR_HI, XL_MDR_LO, XL_MAR, LATCH, NEXT_INST[0], NEXT_INST[1], NEXT_INST[2], NEXT_INST[3], NEXT_INST[4], NEXT_INST[5], NEXT_INST[6], NEXT_INST[7]}),
    .clr(not_1_out));
  not not_1 (not_1_out, nRESET);
  not U14C (nE_MDR_LO, register_1_q[15]);
  or U61B (U61B_out, nFP_WRITE, nDMA_ACQ);
  not U14B (nE_MDR_HI, register_1_q[16]);
  nand U25A (R_RW, U61B_out, nE_MDR_HI, nE_MDR_LO);
endmodule
