// Logisim project RAM_ROM.circ as structural Verilog: 1 circuit, main circuit RAM_ROM
module RAM_ROM (
  input  nWE,
  input  [21:0] A,
  input  nOE,
  input  FP_RAM,
  input  MEMORY,
  output [7:0] DBUS
);

  wire and_1_out, and_2_out, nand_1_out, nand_2_out, nor_1_out, nor_2_out, nor_3_out, not_1_out, or_1_out;

  // NoConnect on {A[21:15], A[13:7]}
  or or_1 (or_1_out, A[14], FP_RAM);
  nor nor_1 (nor_1_out, MEMORY, A[0]);
  nor nor_2 (nor_2_out, A[1], A[2], A[3]);
  nor nor_3 (nor_3_out, A[4], A[5], A[6]);
  RAM62256 ram62256_1 (.nWE(nWE), .A(A[21:7]), .nOE(nOE), .nCS(nand_1_out), .D(DBUS));
  ROM27256 rom27256_1 (.A(A[21:7]), .nCS(nand_2_out), .nOE(nOE), .D(DBUS));
  and and_1 (and_1_out, nor_2_out, nor_3_out);
  nand nand_1 (nand_1_out, and_2_out, or_1_out);
  nand nand_2 (nand_2_out, and_2_out, not_1_out);
  and and_2 (and_2_out, nor_1_out, and_1_out);
  not not_1 (not_1_out, or_1_out);
endmodule
