// Logisim project REGS.circ as structural Verilog: 1 circuit, main circuit REGS
module REGS (
  input  [15:0] Z,
  input  [20:0] L_CTLBUS,
  input  [11:0] nEL_CTLBUS,
  input  nDMA_ACK,
  input  nRW,
  input  [6:0] XL_CTLBUS,
  input  [1:0] nER_CTLBUS,
  input  nRESET,
  input  [1:0] IMMVAL,
  output [15:0] L,
  output [7:0] D,
  output [7:0] DBUS,
  output [15:0] R,
  output [15:0] MAR
);

  // GREGS gregs_1: pin names not known; wires that end beside it: Z, L_CTLBUS[8], L_CTLBUS[9], L_CTLBUS[10], L_CTLBUS[11], L_CTLBUS[12], L_CTLBUS[13], L_CTLBUS[14], L_CTLBUS[15], L_CTLBUS[16], nEL_CTLBUS[7], nEL_CTLBUS[8], nEL_CTLBUS[3], nEL_CTLBUS[4], nEL_CTLBUS[6], nEL_CTLBUS[9], nEL_CTLBUS[10], nEL_CTLBUS[5], L_CTLBUS[5], L
  MDR mdr_1 (
    .L(L), .R(R), .DBUS(DBUS), .D(D), .nE_MDR_LO(XL_CTLBUS[6]), .nE_MDR_HI(XL_CTLBUS[5]),
    .nEL_MDR(nEL_CTLBUS[1]), .nER_MDR(nER_CTLBUS[1]), .nDMA_ACK(nDMA_ACK), .nRW(nRW), .Z(Z),
    .L_MDR_LO(L_CTLBUS[2]), .COMMIT(L_CTLBUS[5]), .L_MDR_HI(L_CTLBUS[3]), .XL_MDR_LO(XL_CTLBUS[1]),
    .XL_MDR_HI(XL_CTLBUS[2]));
  SREGS sregs_1 (
    .L_MAR(L_CTLBUS[4]), .Z(Z), .nRESET(nRESET), .nEL_MAR(nEL_CTLBUS[0]), .IMMVAL(IMMVAL),
    .nER_IMM(nER_CTLBUS[0]), .MAR(MAR), .L(L), .R(R));
endmodule
